# Fritzing sketch Auto Feeder (saved by Fritzing 0.8.7b)
breadboards: 1

parts:
  U1 = NodeMCU V3.0
  J2 = Basic Servo

nets:
  N1: U1.D1, J2.pulse
  N2: U1.GND#6, U1.GND#13, U1.GND#16, U1.GND#33, J2.gnd
  VIN: U1.Vin, J2.vcc

custom parts:
  NodeMCU V3.0: ESP8266 based NodeMCU
