# Fritzing sketch Praktikum 7 - Tugas (saved by Fritzing 0.8.7b)
breadboards: 1

parts:
  U1 = NodeMCU V3.0
  DHT11_1 = DHT11 module
  LED1 = RGB LED (com. anode, rbg) [package="5 mm [THT]"]
  LCM1602_IIC1 = LCM1602 IIC [part_number="LCM1602 IIC" chip_label="LCM1602 IIC" package="DIP (Dual Inline) [THT]"]
  U2 = LCD-16X2 [package=lcd-16x2]

nets:
  N1: U1.D1, LCM1602_IIC1.SCL
  N2: U1.D2, LCM1602_IIC1.SDA
  N3: U1.3V3, LED1.common_anode
  GND: U1.GND#6, U1.GND#13, U1.GND#16, U1.GND#33, DHT11_1.GND, LCM1602_IIC1.GND
  N4: U1.D5, LED1.red_cathode
  N5: U1.D6, LED1.blue_cathode
  N6: U1.D7, LED1.green_cathode
  VIN: U1.Vin, DHT11_1.DATA, LCM1602_IIC1.VCC
  N7: U1.A0, DHT11_1.VCC
  VSS: LCM1602_IIC1.VSS, U2.VSS
  VDD: LCM1602_IIC1.VDD, U2.VDD
  N8: LCM1602_IIC1.V0, U2.VO
  N9: LCM1602_IIC1.RS, U2.RS
  N10: LCM1602_IIC1.RW, U2.R_W
  N11: LCM1602_IIC1.E, U2.E
  N12: LCM1602_IIC1.D0, U2.DB0
  N13: LCM1602_IIC1.D1, U2.DB1
  N14: LCM1602_IIC1.D2, U2.DB2
  N15: LCM1602_IIC1.D3, U2.DB3
  N16: LCM1602_IIC1.D4, U2.DB4
  N17: LCM1602_IIC1.D5, U2.DB5
  N18: LCM1602_IIC1.D6, U2.DB6
  N19: LCM1602_IIC1.D7, U2.DB7
  N20: LCM1602_IIC1.A, U2.A
  N21: LCM1602_IIC1.K, U2.K

custom parts:
  NodeMCU V3.0: ESP8266 based NodeMCU
  DHT11 module: DHT11 black pcb module
  LCM1602 IIC: I2C-Module to use a 1602 or 2004 LCD on with the wire.h libory Serial LCD Modul
