# Fritzing sketch Prasktikum 6 - Tugas 1 (saved by Fritzing 0.8.7b)
breadboards: 1

parts:
  U1 = NodeMCU V1.0
  LED1 = RGB LED (com. anode, rbg) [package="5 mm [THT]"]
  e-radionica_com1 = LM393 LDR breakout [part_number=100027]

nets:
  N1: U1.3V3, LED1.common_anode
  GND: U1.GND, e-radionica_com1.GND
  N2: U1.D5, LED1.red_cathode
  N3: U1.D6, LED1.blue_cathode
  N4: U1.D7, LED1.green_cathode
  VIN: U1.Vin, e-radionica_com1.VCC
  N5: U1.A0, e-radionica_com1.AO

custom parts:
  NodeMCU V1.0: ESP8266 based NodeMCU
