# Fritzing sketch Prasktikum 6 - Tugas 2 (saved by Fritzing 0.8.7b)
breadboards: 1

parts:
  e-radionica_com1 = LM393 LDR breakout [part_number=100027]
  U1 = NodeMCU V1.0
  LED1 = RGB LED (com. anode, rbg) [package="5 mm [THT]"]
  DHT11_1 = DHT11 module

nets:
  N1: e-radionica_com1.VCC, DHT11_1.DATA
  GND: e-radionica_com1.GND, DHT11_1.GND
  N2: e-radionica_com1.AO, U1.A0
  N3: U1.GND, LED1.common_anode
  N4: U1.D5, LED1.red_cathode
  N5: U1.D6, LED1.blue_cathode
  N6: U1.D7, LED1.green_cathode

custom parts:
  NodeMCU V1.0: ESP8266 based NodeMCU
  DHT11 module: DHT11 black pcb module
