# Fritzing sketch skema tugas no 3 (saved by Fritzing 0.8.7b)
breadboards: 1

parts:
  U1 = NodeMCU V1.0
  DHT11_1 = DHT11 module
  LED1 = RGB LED (com. anode, rbg) [package="5 mm [THT]"]

nets:
  N1: U1.D0, LED1.red_cathode
  N2: U1.D2, LED1.blue_cathode
  N3: U1.D3, LED1.green_cathode
  N4: U1.3V3, LED1.common_anode
  N5: U1.GND, DHT11_1.DATA
  N6: U1.D7, DHT11_1.VCC
  VIN: U1.Vin, DHT11_1.GND

custom parts:
  NodeMCU V1.0: ESP8266 based NodeMCU
  DHT11 module: DHT11 black pcb module
